// Logisim project lab3.circ as structural Verilog: 12 circuits, main circuit main
module main (
);

  wire clock_1_out, comparator_1_lt, counter_1_carry, not_1_out, Reset, TClock;
  wire [2:0] rom_1_data;
  wire [3:0] multiplexer_1_out;
  wire [4:0] MSB;
  wire [5:0] counter_1_q;
  wire [6:0] adder_1_out, LSB;
  wire [8:0] R0, R1, R2, R3, R4, R5, R6, R7;

  TTY #(.rows(33), .cols(1)) tty_1 (.data({2'b10, MSB}), .clk(TClock), .clr(Reset));  // open: we
  TTY #(.rows(33), .cols(1)) tty_2 (.data(LSB), .clk(TClock), .clr(Reset));  // open: we
  Button u_Reset (.out(Reset));
  Counter #(.width(6), .max('h20), .ongoal("stay")) counter_1 (
    .Q(counter_1_q), .carry(counter_1_carry), .clk(TClock), .clr(Reset));  // open: load, D, count
  Multiplexer #(.select(3), .width(9), .disabled(0), .enable("false")) multiplexer_1 (
    .in0(R0), .in1(R1), .in2(R2), .in3(R3), .in4(R4), .in5(R5), .in6(R6), .in7(R7),
    .out({MSB, multiplexer_1_out}), .sel(rom_1_data));
  not not_1 (not_1_out, counter_1_carry);
  Clock clock_1 (.out(clock_1_out));
  and and_1 (TClock, not_1_out, clock_1_out);
  ROM #(.addrWidth(6), .dataWidth(3)) rom_1 (.addr(counter_1_q), .data(rom_1_data));  // open: sel
  // Probe on {3'b011, multiplexer_1_out}
  // Probe on {2'b10, MSB}
  Comparator #(.width(7)) comparator_1 (
    .a(7'b0111001), .b({3'b011, multiplexer_1_out}), .lt(comparator_1_lt));  // open: gt, eq
  // Probe on LSB
  Multiplexer #(.width(7), .disabled(0), .enable("false")) multiplexer_2 (
    .in0({3'b011, multiplexer_1_out}), .in1(adder_1_out), .out(LSB), .sel(comparator_1_lt));
  Adder #(.width(7)) adder_1 (.a({3'b011, multiplexer_1_out}), .b(7'b0000111), .out(adder_1_out));  // open: cin, cout

  // Notes on the sheet:
  //   @0
  //   JA
  //   E5
  //   @0
  //   OF
  //   U5
  //   OF
  //   E5
  //   E5
  //   U4
  //   E5
  //   E5
  //   U4
  //   _F
  //   _F
  //   _F
  //   AF
  //   AF
  //   AF
  //   @0
  //   AE
  //   AE
  //   AE
  //   _E
  //   OF
  //   ^0
  //   J9
  //   P1
  //   R0
  //   R0
  //   ^0
  //   _F
  //   contents of rom_1 (hex, n*v repeats v):
  //   0 0 1 2 3 4 5 6 6 2 3 4 5 6 6 0 1 2 3 4 5 6 6 2 3 4 5 6 6 6 7
endmodule

module my_9_bit_CLA (
  input  C0,
  input  p0,
  input  g0,
  input  p1,
  input  g1,
  input  p2,
  input  g2,
  input  p3,
  input  g3,
  input  p4,
  input  g4,
  input  p5,
  input  g5,
  input  p6,
  input  g6,
  input  p7,
  input  g7,
  input  p8,
  input  g8,
  output C1,
  output C2,
  output C3,
  output C4,
  output C5,
  output C6,
  output C7,
  output C8,
  output C9
);

  wire and_1_out, and_2_out, and_3_out, and_4_out, and_5_out, and_6_out, and_7_out, and_8_out, and_9_out,
       and_10_out, and_11_out, and_12_out, and_13_out, and_14_out, and_15_out, and_16_out, and_17_out,
       and_18_out, and_19_out, and_20_out, and_21_out, and_22_out, and_23_out, and_24_out, and_25_out,
       and_26_out, and_27_out, and_28_out, and_29_out, and_30_out, and_31_out, and_32_out, and_33_out,
       and_34_out, and_35_out, and_36_out, and_37_out, and_38_out, and_39_out, and_40_out, and_41_out,
       and_42_out, and_43_out, and_44_out, and_45_out;

  and and_1 (and_1_out, C0, p0);
  and and_2 (and_2_out, g1, p2);
  and and_3 (and_3_out, g0, p1, p2);
  and and_4 (and_4_out, C0, g0, p1, p2);
  and and_5 (and_5_out, g2, p3);
  and and_6 (and_6_out, g1, p2, p3);
  and and_7 (and_7_out, g0, p1, p2, p3);
  and and_8 (and_8_out, C0, p0, p1, p2, p3);
  and and_9 (and_9_out, p4, g3);
  and and_10 (and_10_out, p4, p3, g2);
  and and_11 (and_11_out, p4, p3, p2, g1);
  and and_12 (and_12_out, p4, p3, p2, p1, g0);
  and and_13 (and_13_out, p4, p3, p2, p1, p0, C0);
  and and_14 (and_14_out, p5, g4);
  and and_15 (and_15_out, p5, p4, g3);
  and and_16 (and_16_out, p5, p4, p3, g2);
  and and_17 (and_17_out, p5, p4, p3, p2, g1);
  and and_18 (and_18_out, p5, p4, p3, p2, p1, g0);
  and and_19 (and_19_out, p5, p4, p3, p2, p1, p0, C0);
  and and_20 (and_20_out, p6, g5);
  and and_21 (and_21_out, p6, p5, g4);
  and and_22 (and_22_out, p6, p5, p4, g3);
  and and_23 (and_23_out, p6, p5, p4, p3, g2);
  and and_24 (and_24_out, p6, p5, p4, p3, p2, g1);
  and and_25 (and_25_out, p6, p5, p4, p3, p2, p1, g0);
  and and_26 (and_26_out, p6, p5, p4, p3, p2, p1, p0, C0);
  and and_27 (and_27_out, p7, g6);
  and and_28 (and_28_out, p7, p6, g5);
  and and_29 (and_29_out, p7, p6, p5, g4);
  and and_30 (and_30_out, p7, p6, p5, p4, g3);
  and and_31 (and_31_out, p7, p6, p5, p4, p3, g2);
  and and_32 (and_32_out, p7, p6, p5, p4, p3, p2, g1);
  and and_33 (and_33_out, p7, p6, p5, p4, p3, p2, p1, g0);
  and and_34 (and_34_out, p7, p6, p5, p4, p3, p2, p1, p0, C0);
  and and_35 (and_35_out, p8, g7);
  and and_36 (and_36_out, p8, p7, g6);
  and and_37 (and_37_out, p8, p7, p6, g5);
  and and_38 (and_38_out, p8, p7, p6, p5, g4);
  and and_39 (and_39_out, p8, p7, p6, p5, p4, g3);
  and and_40 (and_40_out, p8, p7, p6, p5, p4, p3, g2);
  and and_41 (and_41_out, p8, p7, p6, p5, p4, p3, p2, g1);
  and and_42 (and_42_out, p8, p7, p6, p5, p4, p3, p2, p1, g0);
  or or_1 (C1, and_1_out, g0);
  and and_43 (and_43_out, g0, p1);
  and and_44 (and_44_out, C0, p0, p1);
  and and_45 (and_45_out, p8, p7, p6, p5, p4, p3, p2, p1, p0, C0);
  or or_2 (C2, g1, and_43_out, and_44_out);
  or or_3 (C3, g2, and_2_out, and_3_out, and_4_out);
  or or_4 (C4, g3, and_5_out, and_6_out, and_7_out, and_8_out);
  or or_5 (C5, g4, and_9_out, and_10_out, and_11_out, and_12_out, and_13_out);
  or or_6 (C6, g5, and_14_out, and_15_out, and_16_out, and_17_out, and_18_out, and_19_out);
  or or_7 (C7, g6, and_20_out, and_21_out, and_22_out, and_23_out, and_24_out, and_25_out, and_26_out);
  or or_8 (C8, g7, and_27_out, and_28_out, and_29_out, and_30_out, and_31_out, and_32_out, and_33_out, and_34_out);
  or or_9 (C9, g8, and_35_out, and_36_out, and_37_out, and_38_out, and_39_out, and_40_out, and_41_out, and_42_out, and_45_out);
endmodule

module my_Full_Adder (
  input  A,
  input  B,
  input  C_in,
  output S,
  output g,
  output p
);

  wire xor_1_out;

  xor xor_1 (xor_1_out, A, B);
  and and_1 (g, A, B);
  xor xor_2 (p, A, B);
  xor xor_3 (S, xor_1_out, C_in);
endmodule

module my_9_bit_Adder (
  input  A8,
  input  B8,
  input  A7,
  input  B7,
  input  A6,
  input  B6,
  input  A5,
  input  B5,
  input  A4,
  input  B4,
  input  A3,
  input  B3,
  input  A2,
  input  B2,
  input  B1,
  input  A1,
  input  C0,
  input  B0,
  input  A0,
  output C9,
  output S8,
  output S7,
  output S6,
  output S5,
  output S4,
  output S3,
  output S2,
  output S1,
  output S0
);

  wire C1, C2, C3, C4, C5, C6, C7, C8, g0, g1, g2, g3, g4, g5, g6, g7, g8, p0, p1, p2, p3, p4, p5, p6, p7, p8;

  my_Full_Adder my_full_adder_1 (.A(B8), .B(A8), .C_in(C8), .S(S8), .g(g8), .p(p8));
  my_9_bit_CLA my_9_bit_cla_1 (
    .C0(C0), .p0(p0), .g0(g0), .p1(p1), .g1(g1), .p2(p2), .g2(g2), .p3(p3), .g3(g3), .p4(p4), .g4(g4),
    .p5(p5), .g5(g5), .p6(p6), .g6(g6), .p7(p7), .g7(g7), .p8(p8), .g8(g8), .C1(C1), .C2(C2), .C3(C3),
    .C4(C4), .C5(C5), .C6(C6), .C7(C7), .C8(C8), .C9(C9));
  my_Full_Adder my_full_adder_2 (.A(B7), .B(A7), .C_in(C7), .S(S7), .g(g7), .p(p7));
  my_Full_Adder my_full_adder_3 (.A(B6), .B(A6), .C_in(C6), .S(S6), .g(g6), .p(p6));
  my_Full_Adder my_full_adder_4 (.A(B5), .B(A5), .C_in(C5), .S(S5), .g(g5), .p(p5));
  my_Full_Adder my_full_adder_5 (.A(B4), .B(A4), .C_in(C4), .S(S4), .g(g4), .p(p4));
  my_Full_Adder my_full_adder_6 (.A(B3), .B(A3), .C_in(C3), .S(S3), .g(g3), .p(p3));
  my_Full_Adder my_full_adder_7 (.A(B2), .B(A2), .C_in(C2), .S(S2), .g(g2), .p(p2));
  my_Full_Adder my_full_adder_8 (.A(A1), .B(B1), .C_in(C1), .S(S1), .g(g1), .p(p1));
  my_Full_Adder my_full_adder_9 (.A(A0), .B(B0), .C_in(C0), .S(S0), .g(g0), .p(p0));
endmodule

module my_9_bit_Subtractor (
  input  B8,
  input  B7,
  input  B6,
  input  B5,
  input  B4,
  input  B3,
  input  B2,
  input  B1,
  input  B0,
  input  A8,
  input  A7,
  input  A6,
  input  A5,
  input  A4,
  input  A3,
  input  A2,
  input  A1,
  input  A0,
  output C9,
  output S8,
  output S7,
  output S6,
  output S5,
  output S4,
  output S3,
  output S2,
  output S1,
  output S0
);

  wire not_1_out, not_2_out, not_3_out, not_4_out, not_5_out, not_6_out, not_7_out, not_8_out, not_9_out;

  not not_1 (not_1_out, B8);
  not not_2 (not_2_out, B7);
  not not_3 (not_3_out, B6);
  not not_4 (not_4_out, B5);
  not not_5 (not_5_out, B4);
  not not_6 (not_6_out, B3);
  not not_7 (not_7_out, B2);
  my_9_bit_Adder my_9_bit_adder_1 (
    .C9(C9), .A8(A8), .B8(not_1_out), .S8(S8), .A7(A7), .B7(not_2_out), .S7(S7), .A6(A6), .B6(not_3_out),
    .S6(S6), .A5(A5), .B5(not_4_out), .S5(S5), .A4(A4), .B4(not_5_out), .S4(S4), .A3(A3), .B3(not_6_out),
    .S3(S3), .A2(A2), .B2(not_7_out), .S2(S2), .B1(not_8_out), .A1(A1), .S1(S1), .C0(1'b1), .B0(not_9_out),
    .S0(S0), .A0(A0));
  not not_8 (not_8_out, B1);
  not not_9 (not_9_out, B0);
endmodule

module ALU (
  input  [3:0] opcode,
  input  [8:0] A,
  input  [8:0] B,
  output [8:0] Result
);

  wire C_in;
  wire [8:0] ADD_Result, AND_Result, NOT_Result, OR_Result, SUB_Result, XOR_Result;

  my_9_bit_Adder my_9_bit_adder_1 (
    .A8(A[8]), .B8(B[8]), .S8(ADD_Result[8]), .A7(A[7]), .B7(B[7]), .S7(ADD_Result[7]), .A6(A[6]), .B6(B[6]),
    .S6(ADD_Result[6]), .A5(A[5]), .B5(B[5]), .S5(ADD_Result[5]), .A4(A[4]), .B4(B[4]), .S4(ADD_Result[4]),
    .A3(A[3]), .B3(B[3]), .S3(ADD_Result[3]), .A2(A[2]), .B2(B[2]), .S2(ADD_Result[2]), .B1(B[1]), .A1(A[1]),
    .S1(ADD_Result[1]), .C0(C_in), .B0(B[0]), .S0(ADD_Result[0]), .A0(A[0]));  // open: C9
  my_9_bit_Subtractor my_9_bit_subtractor_1 (
    .A8(A[8]), .B8(B[8]), .S8(SUB_Result[8]), .A7(A[7]), .B7(B[7]), .S7(SUB_Result[7]), .A6(A[6]), .B6(B[6]),
    .S6(SUB_Result[6]), .A5(A[5]), .B5(B[5]), .S5(SUB_Result[5]), .A4(A[4]), .B4(B[4]), .S4(SUB_Result[4]),
    .A3(A[3]), .B3(B[3]), .S3(SUB_Result[3]), .A2(A[2]), .B2(B[2]), .S2(SUB_Result[2]), .B1(B[1]), .A1(A[1]),
    .S1(SUB_Result[1]), .B0(B[0]), .S0(SUB_Result[0]), .A0(A[0]));  // open: C9
  not not_1 (NOT_Result[0], A[0]);
  not not_2 (NOT_Result[1], A[1]);
  not not_3 (NOT_Result[2], A[2]);
  not not_4 (NOT_Result[3], A[3]);
  not not_5 (NOT_Result[4], A[4]);
  not not_6 (NOT_Result[5], A[5]);
  not not_7 (NOT_Result[6], A[6]);
  not not_8 (NOT_Result[7], A[7]);
  not not_9 (NOT_Result[8], A[8]);
  and and_1 (AND_Result[0], A[0], B[0]);
  and and_2 (AND_Result[1], A[1], B[1]);
  and and_3 (AND_Result[2], A[2], B[2]);
  and and_4 (AND_Result[3], A[3], B[3]);
  and and_5 (AND_Result[4], A[4], B[4]);
  and and_6 (AND_Result[5], A[5], B[5]);
  and and_7 (AND_Result[6], A[6], B[6]);
  and and_8 (AND_Result[7], A[7], B[7]);
  and and_9 (AND_Result[8], A[8], B[8]);
  or or_1 (OR_Result[0], A[0], B[0]);
  or or_2 (OR_Result[1], A[1], B[1]);
  or or_3 (OR_Result[2], A[2], B[2]);
  or or_4 (OR_Result[3], A[3], B[3]);
  or or_5 (OR_Result[4], A[4], B[4]);
  or or_6 (OR_Result[5], A[5], B[5]);
  or or_7 (OR_Result[6], A[6], B[6]);
  or or_8 (OR_Result[7], A[7], B[7]);
  or or_9 (OR_Result[8], A[8], B[8]);
  xor xor_1 (XOR_Result[0], A[0], B[0]);
  xor xor_2 (XOR_Result[1], A[1], B[1]);
  xor xor_3 (XOR_Result[2], A[2], B[2]);
  xor xor_4 (XOR_Result[3], A[3], B[3]);
  xor xor_5 (XOR_Result[4], A[4], B[4]);
  xor xor_6 (XOR_Result[5], A[5], B[5]);
  xor xor_7 (XOR_Result[6], A[6], B[6]);
  xor xor_8 (XOR_Result[7], A[7], B[7]);
  xor xor_9 (XOR_Result[8], A[8], B[8]);
  Multiplexer #(.select(4), .width(9)) multiplexer_1 (
    .in2(NOT_Result), .in3(AND_Result), .in4(OR_Result), .in5(XOR_Result), .in6(ADD_Result),
    .in7(SUB_Result), .in8({A[7:0], 1'b0}), .in9({1'b0, A[8:1]}), .out(Result), .sel(opcode));  // open: in0, in1, in10, in11, in12, in13, in14, in15, en
  // also tied to GND on the sheet: {A[0], A[8]}

  // Other names for the same wires on the sheet: SLL_Result[8:1] = A[7:0]; SRL_Result[7:0] = A[8:1]
endmodule

module CLU (
  input  Write_Enable,
  input  Reset
);

  wire Clock;
  wire [2:0] A;
  wire [3:0] ALU_opcode, B, B_OUT, Opcode;
  wire [5:0] n6_bit_counter_1_count;
  wire [7:0] Register_File_select;
  wire [8:0] alu_1_result, Data, muxes_1_a_out_to_alu, muxes_1_b_out_to_alu, register_file_1_r0,
       register_file_1_r1, register_file_1_r2, register_file_1_r3, register_file_1_r4, register_file_1_r5,
       register_file_1_r6, register_file_1_r7;
  wire [18:16] ram_1_data;

  Clock clock_1 (.out(Clock));
  _6_bit_counter u_6_bit_counter_1 (.Clock(Clock), .reset(Reset), .count(n6_bit_counter_1_count));
  Control_Unit control_unit_1 (
    .Opcode(Opcode), .ALU_Select(ALU_opcode), .B_in(B), .B_out(B_OUT), .Write_Enable(Write_Enable));
  RAM #(.addrWidth(6), .dataWidth(23), .bus("separate")) ram_1 (
    .addr(n6_bit_counter_1_count), .data({Opcode, ram_1_data, A, B, Data}), .clk(Clock));  // open: din, str, sel, ld, clr
  Decoder #(.select(3)) decoder_1 (
    .out0(Register_File_select[0]), .out1(Register_File_select[1]), .out2(Register_File_select[2]),
    .out3(Register_File_select[3]), .out4(Register_File_select[4]), .out5(Register_File_select[5]),
    .out6(Register_File_select[6]), .out7(Register_File_select[7]), .sel(ram_1_data));  // open: en
  Muxes muxes_1 (
    .A_Select_in(A), .A_out_to_ALU(muxes_1_a_out_to_alu), .B_out_to_ALU(muxes_1_b_out_to_alu),
    .R0(register_file_1_r0), .R1(register_file_1_r1), .R2(register_file_1_r2), .R3(register_file_1_r3),
    .R4(register_file_1_r4), .R5(register_file_1_r5), .R6(register_file_1_r6), .R7(register_file_1_r7),
    .DATA_IN(Data), .B_Select_in(B_OUT));
  ALU alu_1 (.opcode(ALU_opcode), .A(muxes_1_a_out_to_alu), .B(muxes_1_b_out_to_alu), .Result(alu_1_result));
  Register_File register_file_1 (
    .Clock(Clock), .Write_Enable(Write_Enable), .Reset(Reset), .I0(alu_1_result), .I1(alu_1_result),
    .I2(alu_1_result), .I3(alu_1_result), .I4(alu_1_result), .I5(alu_1_result), .I6(alu_1_result),
    .I7(alu_1_result), .Select_bits(Register_File_select), .R0(register_file_1_r0), .R1(register_file_1_r1),
    .R2(register_file_1_r2), .R3(register_file_1_r3), .R4(register_file_1_r4), .R5(register_file_1_r5),
    .R6(register_file_1_r6), .R7(register_file_1_r7));
endmodule

module _6_bit_counter (
  input  Clock,
  input  reset,
  output [5:0] count
);

  wire and_1_out, and_2_out, and_3_out, and_4_out;

  T_Flip_Flop t_ff_1 (.clk(Clock), .T(1'b1), .Q(count[5]), .reset(reset));  // open: Qn, preset, en
  T_Flip_Flop t_ff_2 (.clk(Clock), .T(count[5]), .Q(count[4]), .reset(reset));  // open: Qn, preset, en
  and and_1 (and_1_out, count[4], count[5]);
  T_Flip_Flop t_ff_3 (.clk(Clock), .T(and_1_out), .Q(count[3]), .reset(reset));  // open: Qn, preset, en
  and and_2 (and_2_out, count[3], and_1_out);
  T_Flip_Flop t_ff_4 (.clk(Clock), .T(and_2_out), .Q(count[2]), .reset(reset));  // open: Qn, preset, en
  and and_3 (and_3_out, count[2], and_2_out);
  T_Flip_Flop t_ff_5 (.clk(Clock), .T(and_3_out), .Q(count[1]), .reset(reset));  // open: Qn, preset, en
  and and_4 (and_4_out, count[1], and_3_out);
  T_Flip_Flop t_ff_6 (.clk(Clock), .T(and_4_out), .Q(count[0]), .reset(reset));  // open: Qn, preset, en
endmodule

module Control_Unit (
  input  [3:0] Opcode,
  input  [3:0] B_in,
  output [3:0] ALU_Select,
  output [3:0] B_out,
  output Write_Enable
);
endmodule

module _9_bit_register (
  input  [8:0] Register_Input,
  input  Clock,
  input  Enable,
  input  Reset,
  output [8:0] Output
);

  D_Flip_Flop d_ff_1 (
    .clk(Clock), .D(Register_Input[0]), .Q(Output[0]), .en(Enable), .reset(Reset));  // open: Qn, preset
  D_Flip_Flop d_ff_2 (
    .clk(Clock), .D(Register_Input[1]), .Q(Output[1]), .en(Enable), .reset(Reset));  // open: Qn, preset
  D_Flip_Flop d_ff_3 (
    .clk(Clock), .D(Register_Input[2]), .Q(Output[2]), .en(Enable), .reset(Reset));  // open: Qn, preset
  D_Flip_Flop d_ff_4 (
    .clk(Clock), .D(Register_Input[6]), .Q(Output[6]), .en(Enable), .reset(Reset));  // open: Qn, preset
  D_Flip_Flop d_ff_5 (
    .clk(Clock), .D(Register_Input[7]), .Q(Output[7]), .en(Enable), .reset(Reset));  // open: Qn, preset
  D_Flip_Flop d_ff_6 (
    .clk(Clock), .D(Register_Input[8]), .Q(Output[8]), .en(Enable), .reset(Reset));  // open: Qn, preset
  D_Flip_Flop d_ff_7 (
    .clk(Clock), .D(Register_Input[3]), .Q(Output[3]), .en(Enable), .reset(Reset));  // open: Qn, preset
  D_Flip_Flop d_ff_8 (
    .clk(Clock), .D(Register_Input[4]), .Q(Output[4]), .en(Enable), .reset(Reset));  // open: Qn, preset
  D_Flip_Flop d_ff_9 (
    .clk(Clock), .D(Register_Input[5]), .Q(Output[5]), .en(Enable), .reset(Reset));  // open: Qn, preset
endmodule

module Register_File (
  input  Clock,
  input  Write_Enable,
  input  Reset,
  input  [8:0] I0,
  input  [8:0] I1,
  input  [8:0] I2,
  input  [8:0] I3,
  input  [8:0] I4,
  input  [8:0] I5,
  input  [8:0] I6,
  input  [8:0] I7,
  input  [7:0] Select_bits,
  output [8:0] R0,
  output [8:0] R1,
  output [8:0] R2,
  output [8:0] R3,
  output [8:0] R4,
  output [8:0] R5,
  output [8:0] R6,
  output [8:0] R7
);

  wire S0, S1, S2, S3, S4, S5, S6, S7;

  _9_bit_register u_9_bit_register_1 (.Register_Input(I0), .Clock(Clock), .Enable(S0), .Reset(Reset), .Output(R0));
  _9_bit_register u_9_bit_register_2 (.Register_Input(I1), .Clock(Clock), .Enable(S1), .Reset(Reset), .Output(R1));
  _9_bit_register u_9_bit_register_3 (.Register_Input(I2), .Clock(Clock), .Enable(S2), .Reset(Reset), .Output(R2));
  _9_bit_register u_9_bit_register_4 (.Register_Input(I3), .Clock(Clock), .Enable(S3), .Reset(Reset), .Output(R3));
  _9_bit_register u_9_bit_register_5 (.Register_Input(I4), .Clock(Clock), .Enable(S4), .Reset(Reset), .Output(R4));
  _9_bit_register u_9_bit_register_6 (.Register_Input(I5), .Clock(Clock), .Enable(S5), .Reset(Reset), .Output(R5));
  _9_bit_register u_9_bit_register_7 (.Register_Input(I6), .Clock(Clock), .Enable(S6), .Reset(Reset), .Output(R6));
  _9_bit_register u_9_bit_register_8 (.Register_Input(I7), .Clock(Clock), .Enable(S7), .Reset(Reset), .Output(R7));
  and and_1 (S0, Select_bits[0], Write_Enable);
  and and_2 (S1, Select_bits[1], Write_Enable);
  and and_3 (S2, Select_bits[2], Write_Enable);
  and and_4 (S3, Select_bits[3], Write_Enable);
  and and_5 (S4, Select_bits[4], Write_Enable);
  and and_6 (S5, Select_bits[5], Write_Enable);
  and and_7 (S6, Select_bits[6], Write_Enable);
  and and_8 (S7, Select_bits[7], Write_Enable);
endmodule

module Muxes (
  input  [8:0] R0,
  input  [8:0] R1,
  input  [8:0] R2,
  input  [8:0] R3,
  input  [8:0] R4,
  input  [8:0] R5,
  input  [8:0] R6,
  input  [8:0] R7,
  input  [8:0] DATA_IN,
  input  [2:0] A_Select_in,
  input  [3:0] B_Select_in,
  output [8:0] A_out_to_ALU,
  output [8:0] B_out_to_ALU
);

  Multiplexer #(.select(3), .width(9)) multiplexer_1 (
    .in0(R0), .in1(R1), .in2(R2), .in3(R3), .in4(R4), .in5(R5), .in6(R6), .in7(R7), .out(A_out_to_ALU),
    .sel(A_Select_in));  // open: en
  Multiplexer #(.select(4), .width(9)) multiplexer_2 (
    .in0(R0), .in1(R1), .in2(R2), .in3(R3), .in4(R4), .in5(R5), .in6(R6), .in7(R7), .in8(DATA_IN),
    .out(B_out_to_ALU), .sel(B_Select_in));  // open: in9, in10, in11, in12, in13, in14, in15, en
endmodule
